# Fritzing sketch Mioduino (saved by Fritzing 0.9.2b)
circuit board: 8.46667cm x 5.64444cm

parts:
  U1 = atmega328 [package=dip]
  S1 = Momentary Switch [package=ksa_sealed_tac_switch]
  7805 = Voltage Regulator - 5V [package="TO220 [THT]"]
  C2 = Electrolytic Capacitor [capacitance=47µF package="1010 [SMD, electrolytic]"]
  R1 = Resistor [tolerance=±5% resistance=1k package=THT]
  R2 = Resistor [tolerance=±5% resistance=1k package=THT]
  LED2 = LED - 3mm [color="Green (555nm)" package="3 mm [THT]"]
  LED1 = LED - 3mm [color="Red (635nm)" package="3 mm [THT]"]
  XTAL1 = Crystal [frequency="16 Mhz" package=THT]
  R3 = Resistor [tolerance=±5% resistance=10k package="0603 [SMD]"]
  C8 = Ceramic Capacitor [capacitance=0.1µF package="0603 [SMD, multilayer]"]
  C1 = Ceramic Capacitor [capacitance=0.1µF package="0603 [SMD, multilayer]"]
  C3 = Ceramic Capacitor [capacitance=0.1µF package="0603 [SMD, multilayer]"]
  C5 = Electrolytic Capacitor [capacitance=100µF package="1010 [SMD, electrolytic]"]
  D1 = Rectifier Diode [part_number=1N4001 package="Melf DO-213 AB [SMD]"]
  C7 = Ceramic Capacitor [capacitance=20pF package="100 mil [THT, multilayer]"]
  JP1 = Header 6 [package=1x06-smd]
  C6 = Ceramic Capacitor [capacitance=20pF package="100 mil [THT, multilayer]"]
  C4 = Ceramic Capacitor [capacitance=0.1µF package="0603 [SMD, multilayer]"]
  D2 = Rectifier Diode [part_number=1N4001 package="Melf DO-213 AB [SMD]"]
  J1 = Power Jack [package=power_jack_pth]

nets:
  N1: U1.RESET, S1.4, R3.Pin_1, C8.1
  N2: U1.D0_(RX), JP1.3
  N3: U1.D1_(TX), JP1.2
  5V: U1.VCC, U1.AVCC, U1.AREF, 7805.output_voltage, R1.Pin_1, R3.Pin_0, C3.1, C5.+, C4.1, D2.cathode
  GND: U1.GND, S1.2, 7805.GND, C2.-, LED2.cathode, LED1.cathode, C1.0, C3.0, C5.-, C7.1, JP1.5, JP1.6, C6.1, C4.0, J1.GND
  N4: U1.XLAT1, XTAL1.pin_0, C6.0
  N5: U1.XLAT2, XTAL1.pin_1, C7.0
  N6: U1.D13, R2.Pin_0
  N7: 7805.input_voltage, C2.+, C1.1, D1.cathode
  N8: R1.Pin_0, LED1.anode
  N9: R2.Pin_1, LED2.anode
  N10: C8.0, JP1.1
  N11: D1.anode, J1.PWR
  N12: JP1.4, D2.anode

notes:
  Mioduino, Schematic diagram for the Mioduino by Daniel Porrey, 1.04
  5V Power Supply
  Reset
  FTDI Interface
  Clock
  Power LED
  Activity LED
